# Fritzing sketch wiring (saved by Fritzing 0.9.3b)

parts:
  HC-SR04_Sensor_1 = HC-SR04 Ultrasonic Distance Sensor
  U1 = Vibration Motor- ROB-08449 [package=vibe-motor-10mm]  # not connected
  Part3 = Arduino Nano (Rev3.0)
  U2 = Vibration Motor- ROB-08449 [package=vibe-motor-10mm]

nets:
  VCC: HC-SR04_Sensor_1.VCC, Part3.5V
  N1: HC-SR04_Sensor_1.TRIG, Part3.D11/MOSI
  N2: HC-SR04_Sensor_1.ECHO, Part3.D10
  GND: HC-SR04_Sensor_1.GND, Part3.GND, U2.+
  N3: Part3.D13/SCK, U2.-
