# Fritzing sketch wiring_v2 (saved by Fritzing 0.9.3b)

parts:
  HC-SR04_Sensor_1 = HC-SR04 Ultrasonic Distance Sensor
  U1 = Vibration Motor- ROB-08449 [package=vibe-motor-10mm]  # not connected
  Part3 = Arduino Nano (Rev3.0)
  U2 = Vibration Motor- ROB-08449 [package=vibe-motor-10mm]
  M1 = TP4056 Module [part_number=HW-107]
  BAT1 = Battery Holders [package=lipo-1100mAh]
  U3 = DC-DC 2-24V Step Up Booster [package=THT]

nets:
  VCC: HC-SR04_Sensor_1.VCC, Part3.5V, U3.pin1
  N1: HC-SR04_Sensor_1.TRIG, Part3.D11/MOSI
  N2: HC-SR04_Sensor_1.ECHO, Part3.D10
  GND: HC-SR04_Sensor_1.GND, Part3.GND, U2.+, U3.pin2
  N3: Part3.D13/SCK, U2.-
  N4: M1.pin2, U3.pin4
  N5: M1.pin3, BAT1.-
  N6: M1.pin4, BAT1.+
  N7: M1.pin5, U3.pin3

custom parts:
  TP4056 Module: TP4056 Lithium Battery Charge Management Module Links: TP4056 website
  DC-DC 2-24V Step Up Booster: Convertisseur DC-DC 2-24V 2A
