# Fritzing sketch wiring_v3 (saved by Fritzing 0.9.3b)

parts:
  HC-SR04_Sensor_1 = HC-SR04 Ultrasonic Distance Sensor
  Part3 = Arduino Nano (Rev3.0)
  U2 = Vibration Motor- ROB-08449 [package=vibe-motor-10mm]
  M1 = TP4056 Module [part_number=HW-107]
  BAT1 = Battery Holders [package=lipo-1100mAh]
  U3 = DC-DC 2-24V Step Up Booster [package=THT]
  S1 = Pushbutton [package="[THT]"]
  U4 = MLX90614 [package=to-39]

nets:
  VCC: HC-SR04_Sensor_1.VCC, Part3.5V, U3.pin1, U4.SCL_VZ
  N1: HC-SR04_Sensor_1.TRIG, Part3.D11/MOSI
  N2: HC-SR04_Sensor_1.ECHO, Part3.D10
  GND: HC-SR04_Sensor_1.GND, Part3.GND, U2.+, U3.pin2, S1.Pin_1, S1.Pin_2, U4.PWM_SDA
  N3: Part3.D12/MISO, U4.VSS
  N4: Part3.A0, S1.Pin_3, S1.Pin_4
  N5: Part3.D13/SCK, U2.-
  N6: M1.pin2, U3.pin4
  N7: M1.pin3, BAT1.-
  N8: M1.pin4, BAT1.+
  N9: M1.pin5, U3.pin3

custom parts:
  TP4056 Module: TP4056 Lithium Battery Charge Management Module Links: TP4056 website
  DC-DC 2-24V Step Up Booster: Convertisseur DC-DC 2-24V 2A
